# Fritzing sketch Amplifier_Schematic (saved by Fritzing 0.9.2b)
circuit board: 5cm x 5cm
breadboards: 1

parts:
  IC1 = TDA7052a [part_number=7052 package="DIP (Dual Inline) [THT]"]
  TRS1 = Audio Jack (TRS) 3.5mm [package="4Ucon 08780 [THT]"]
  SPKR1 = Loudspeaker
  C1 = Electrolytic Capacitor [capacitance=1µF package="100 mil [THT, electrolytic]"]
  C2 = Electrolytic Capacitor [capacitance=1µF package="100 mil [THT, electrolytic]"]
  C3 = Electrolytic Capacitor [capacitance=1µF package="100 mil [THT, electrolytic]"]
  R1 = Resistor [tolerance=±5% resistance=220 package=THT]
  VCC1 = Battery

nets:
  N1: IC1.pin_1, C1.+, C2.+, VCC1.+
  N2: IC1.pin2, C3.+, R1.Pin_0
  GND: IC1.pin3, IC1.pin6, TRS1.Sleeve, C1.-, C2.-, R1.Pin_1
  N3: IC1.pin5, SPKR1.pin1
  N4: IC1.pin8, SPKR1.pin2
  N5: TRS1.Ring, C3.-
  N6: TRS1.Tip, VCC1.-

custom parts:
  TDA7052a: Audio Amplifier
